# Fritzing sketch 회로도 (saved by Fritzing 0.9.6b)
breadboards: 1

parts:
  Raspberry_Pi_1 = Raspberry Pi 3 [part_number=RPI-3-V1.2]
  Grove1 = Grove OLED 128x96
  U1 = TCM8240MD [package=tcm8240md]  # not connected
  J1 = Piezo Speaker
  LED1 = smd LED [color="White (6500K)" package="0805 [SMD]"]
  S1 = Momentary Switch [package=ksa_sealed_tac_switch]
  S2 = Momentary Switch [package=ksa_sealed_tac_switch]
  S3 = Momentary Switch [package=ksa_sealed_tac_switch]
  R1 = Resistor [tolerance=±5% resistance=220 package="2010 [SMD]"]

nets:
  3V3: Raspberry_Pi_1.3v3, Grove1.VCC, S1.2, S2.2, S3.2
  N1: Raspberry_Pi_1.GPIO2, Grove1.SDA
  N2: Raspberry_Pi_1.GPIO3, Grove1.SCL
  N3: Raspberry_Pi_1.GIPO10, S2.4
  N4: Raspberry_Pi_1.GIPO9, S3.4
  N5: Raspberry_Pi_1.GIPO11, S1.4
  GND: Raspberry_Pi_1.GND, Grove1.GND, J1.pin1, LED1.cathode
  N6: Raspberry_Pi_1.GIPO21, R1.Pin_1
  N7: Raspberry_Pi_1.GIPO15, J1.pin2
  N8: LED1.anode, R1.Pin_0
